# Fritzing sketch Checkin-device (saved by Fritzing 0.9.3b)

parts:
  Part1 = Adafruit PN532 NFC RFID Controller Shield [part_number="Adafruit #789"]
  Part2 = Arduino MKR1000
  LED1 = LED - 5mm [color="Red (633nm)" package="5 mm [THT]"]
  J1 = Piezo Speaker

nets:
  GND: Part1.GND, Part2.GND, LED1.cathode, J1.pin1
  N1: Part1.5.0V, Part2.5V
  N2: Part1.SCL, Part2.D12_SCL
  N3: Part1.SDA, Part2.D11_SDA
  N4: Part1.D2, Part2.D2_PWM
  N5: Part2.D6, LED1.anode
  N6: Part2.D10_MISO, J1.pin2

custom parts:
  Adafruit PN532 NFC RFID Controller Shield: We've taken our popular Adafruit PN532 breakout board and turned it into a shield - the perfect tool for any 13.56MHz RFID or NFC application. The Adafruit NFC shield uses the PN532 chip-set (the most popular NFC chip on the market) and is what is embedded in pretty much every phone or device that does NFC. This chipset is very powerful, and can pretty much do it all, such as read and write to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
  Arduino MKR1000: MKR1000 is a powerful board that combines the functionality of the Zero and the Wi-Fi Shield. It is the ideal solution for makers wanting to design IoT projects with minimal previous experience in networking
